// Logisim project final_viva_cpu.circ as structural Verilog: 19 circuits, main circuit main
module main (
  input  RAM_A_OE,
  input  RAM_A_WE,
  input  RAM_B_OE,
  input  RAM_B_WE,
  input  Inst_RAM_OE,
  input  Inst_RAM_WE,
  input  System_RAM_OE,
  input  System_RAM_WE,
  input  MBR_B_WE,
  input  MBR_A_WE,
  input  MBR_Z_WE,
  input  INST_SPL_WE,
  input  MBR_B_CB,
  input  MBR_A_CB,
  input  MBR_Z_CB,
  input  MAR_Z_WE,
  input  MAR_A_WE,
  input  MAR_B_WE,
  input  Reg_8_WE,
  input  Reg_2_WE,
  input  Reg_4_WE,
  input  Reg_6_WE,
  input  Reg_7_WE,
  input  Reg_5_WE,
  input  Reg_3_WE,
  input  Reg_1_WE,
  input  Reg_A_out_CB,
  input  Reg_B_out_CB,
  input  ALU_out_CB,
  input  counter_increment_by_1,
  input  counter_increment_on,
  input  counter_reset,
  input  oppcode_reg_we,
  input  oppcode_reg_cb,
  input  Reg_5_CB,
  input  alu_output_reg_WE,
  input  overflow_reg_WE,
  input  bus_terminal_OE,
  input  selector_b1,
  input  selector_b2,
  input  bus_term_ramB_CB,
  input  bus_term_ramA_CB,
  input  bus_term_ramsys_CB,
  input  bus_term_raminst_CB,
  input  overflow_reg_CB,
  input  alu_reg_cb,
  input  mbr_A_swap_cb,
  input  of_sub_cb,
  input  mbr_B_swap_cb,
  input  of_add_cb,
  input  temp_WE,
  input  mar_c_r,
  input  temp_CB,
  input  mar_c_i_on,
  input  mar_c_i1,
  input  ans1_cb,
  input  ans2_cb,
  input  ans3_cb,
  input  ans4_cb,
  input  ans_finalcb,
  input  ans_finalwe,
  input  sys_ram_cb
);

  wire alu_1_overflow, alu_1_overflow_sub, clock_1_out, not_1_out;
  wire [0:0] controlled_buffer_3_out;
  wire [3:0] ROM_Clock_Counter_q;
  wire [4:0] controlled_buffer_2_out, counter_1_q, counter_2_q, counter_3_q, counter_4_q,
       instructionsplitter_1_add_a, instructionsplitter_1_add_b;
  wire [4:4] instructionsplitter_1_opcode;
  wire [5:0] register_1_q;
  wire [5:5] controlled_buffer_2_out_2;
  wire [15:0] alu_1_out_4, alu_register_q, bus_terminal_1_ram_a, bus_terminal_1_ram_b,
       bus_terminal_1_ram_inst, bus_terminal_1_ram_system, controlled_buffer_1_out, controlled_buffer_6_out,
       controlled_buffer_7_out, controlled_buffer_8_out, controlled_buffer_9_out, controlled_buffer_16_out,
       controlled_buffer_17_out, controlled_buffer_18_out, matmult_1_ans1, matmult_1_ans2, matmult_1_ans3,
       matmult_1_ans4, matmult_output_q, overflow_reg_q, ram_1_dout, ram_2_dout, ram_3_dout, ram_4_dout,
       register_2_q, register_3_q, register_4_q, register_5_q, register_6_q, register_7_q, register_8_q,
       register_9_q, register_10_q, register_11_q, register_12_q, register_13_q, register_14_q,
       register_15_q, temp_q;
  wire [63:0] rom_1_data;

  Counter #(.max('h1f), .width(5)) counter_1 (
    .clr(rom_1_data[32]), .up(rom_1_data[33]), .count(rom_1_data[34]), .clk(clock_1_out), .Q(counter_1_q));  // open: load, D, carry
  Register #(.width(6)) register_1 (
    .D({controlled_buffer_2_out_2[5], controlled_buffer_2_out}), .en(rom_1_data[31]), .clk(clock_1_out),
    .Q(register_1_q));  // open: clr
  // Probe on {controlled_buffer_2_out_2[5], controlled_buffer_2_out}
  Register #(.width(16)) alu_register (
    .D(controlled_buffer_6_out), .en(rom_1_data[28]), .clk(clock_1_out), .Q(alu_register_q));  // open: clr
  Register #(.width(16)) overflow_reg (
    .D({{15{1'b0}}, controlled_buffer_3_out[0]}), .en(rom_1_data[27]), .clk(clock_1_out), .Q(overflow_reg_q));  // open: clr
  assign controlled_buffer_1_out = rom_1_data[18] ? alu_register_q : 16'bz;  // Controlled_Buffer controlled_buffer_1
  assign {controlled_buffer_2_out_2[5], controlled_buffer_2_out} = rom_1_data[30] ? {6{1'b0}} : 6'bz;  // Controlled_Buffer controlled_buffer_2
  ALU alu_1 (
    .A(controlled_buffer_7_out), .opcode(controlled_buffer_2_out), .B(controlled_buffer_8_out),
    .out_4(alu_1_out_4), .overflow(alu_1_overflow), .overflow_sub(alu_1_overflow_sub));
  assign controlled_buffer_3_out[0] = rom_1_data[12] ? alu_1_overflow_sub : 1'bz;  // Controlled_Buffer controlled_buffer_3
  assign controlled_buffer_1_out = rom_1_data[19] ? overflow_reg_q : 16'bz;  // Controlled_Buffer controlled_buffer_4
  // Probe on alu_1_out_4
  assign controlled_buffer_3_out[0] = rom_1_data[11] ? alu_1_overflow : 1'bz;  // Controlled_Buffer controlled_buffer_5
  assign controlled_buffer_6_out = rom_1_data[35] ? alu_1_out_4 : 16'bz;  // Controlled_Buffer controlled_buffer_6
  Counter #(.max('h1f), .width(5)) counter_2 (
    .clr(rom_1_data[10]), .load(rom_1_data[48]), .up(rom_1_data[9]), .count(rom_1_data[8]),
    .clk(clock_1_out), .D(instructionsplitter_1_add_a), .Q(counter_2_q));  // open: carry
  // Probe on instructionsplitter_1_add_b
  Register #(.width(16)) register_2 (
    .D(controlled_buffer_8_out), .en(rom_1_data[38]), .clk(clock_1_out), .Q(register_2_q));  // open: clr
  Register #(.width(16)) register_3 (
    .D(controlled_buffer_8_out), .en(rom_1_data[39]), .clk(clock_1_out), .Q(register_3_q));  // open: clr
  Register #(.width(16)) register_4 (
    .D(controlled_buffer_9_out), .en(rom_1_data[40]), .clk(clock_1_out), .Q(register_4_q));  // open: clr
  Register #(.width(16)) register_5 (
    .D(controlled_buffer_9_out), .en(rom_1_data[41]), .clk(clock_1_out), .Q(register_5_q));  // open: clr
  InstructionSplitter instructionsplitter_1 (
    .Instruction(controlled_buffer_1_out), .Write_Enable(rom_1_data[52]), .clock(clock_1_out),
    .Add_B(instructionsplitter_1_add_b), .Add_A(instructionsplitter_1_add_a),
    .Opcode({instructionsplitter_1_opcode[4], controlled_buffer_2_out[3:0]}),
    .flag(controlled_buffer_2_out[4]));
  // Probe on instructionsplitter_1_add_a
  // Probe on {instructionsplitter_1_opcode[4], controlled_buffer_2_out[3:0]}
  Register #(.width(16)) register_6 (
    .D(controlled_buffer_8_out), .en(rom_1_data[44]), .clk(clock_1_out), .Q(register_6_q));  // open: clr
  // Probe on counter_1_q
  Register #(.width(16)) register_7 (
    .D(controlled_buffer_8_out), .en(rom_1_data[43]), .clk(clock_1_out), .Q(register_7_q));  // open: clr
  Register #(.width(16)) register_8 (
    .D(controlled_buffer_9_out), .en(rom_1_data[42]), .clk(clock_1_out), .Q(register_8_q));  // open: clr
  Register #(.width(16)) register_9 (
    .D(controlled_buffer_9_out), .en(rom_1_data[45]), .clk(clock_1_out), .Q(register_9_q));  // open: clr
  Counter #(.max('h1f), .width(5)) counter_3 (
    .clr(rom_1_data[10]), .load(rom_1_data[47]), .up(rom_1_data[9]), .count(rom_1_data[8]),
    .clk(clock_1_out), .D(instructionsplitter_1_add_a), .Q(counter_3_q));  // open: carry
  assign controlled_buffer_7_out = rom_1_data[37] ? register_7_q : 16'bz;  // Controlled_Buffer controlled_buffer_7
  assign controlled_buffer_8_out = rom_1_data[36] ? register_9_q : 16'bz;  // Controlled_Buffer controlled_buffer_8
  Register #(.width(16)) temp (
    .D(controlled_buffer_7_out), .en(rom_1_data[14]), .clk(clock_1_out), .Q(temp_q));  // open: clr
  Counter #(.max('h1f), .width(5)) counter_4 (
    .clr(rom_1_data[10]), .load(rom_1_data[46]), .up(rom_1_data[9]), .count(rom_1_data[8]),
    .clk(clock_1_out), .D(instructionsplitter_1_add_b), .Q(counter_4_q));  // open: carry
  Register #(.width(16)) register_10 (
    .D(ram_1_dout), .en(rom_1_data[53]), .clk(clock_1_out), .Q(register_10_q));  // open: clr
  Register #(.width(16)) register_11 (
    .D(ram_2_dout), .en(rom_1_data[54]), .clk(clock_1_out), .Q(register_11_q));  // open: clr
  Register #(.width(16)) register_12 (
    .D(ram_4_dout), .en(rom_1_data[55]), .clk(clock_1_out), .Q(register_12_q));  // open: clr
  assign controlled_buffer_9_out = rom_1_data[13] ? temp_q : 16'bz;  // Controlled_Buffer controlled_buffer_9
  assign controlled_buffer_1_out = rom_1_data[49] ? register_10_q : 16'bz;  // Controlled_Buffer controlled_buffer_10
  Clock clock_1 (.out(clock_1_out));
  assign controlled_buffer_8_out = rom_1_data[50] ? register_11_q : 16'bz;  // Controlled_Buffer controlled_buffer_11
  assign controlled_buffer_1_out = rom_1_data[16] ? controlled_buffer_8_out : 16'bz;  // Controlled_Buffer controlled_buffer_12
  assign controlled_buffer_9_out = rom_1_data[51] ? register_12_q : 16'bz;  // Controlled_Buffer controlled_buffer_13
  assign controlled_buffer_1_out = rom_1_data[15] ? controlled_buffer_9_out : 16'bz;  // Controlled_Buffer controlled_buffer_14
  // Probe on controlled_buffer_1_out
  // Probe on counter_1_q
  RAM #(.addrWidth(5), .dataWidth(16), .\type ("nonvolatile")) ram_1 (
    .addr(counter_1_q), .we(rom_1_data[58]), .oe(rom_1_data[59]), .clk(clock_1_out),
    .din(controlled_buffer_1_out), .dout(ram_1_dout));
  assign controlled_buffer_1_out = rom_1_data[20] ? bus_terminal_1_ram_inst : 16'bz;  // Controlled_Buffer controlled_buffer_15
  matmult matmult_1 (
    .reg1(register_2_q), .reg2(register_6_q), .reg3(register_3_q), .reg4(controlled_buffer_7_out),
    .reg5(register_4_q), .reg6(register_8_q), .reg7(register_5_q), .reg8(controlled_buffer_8_out),
    .ans1(matmult_1_ans1), .ans2(matmult_1_ans2), .ans3(matmult_1_ans3), .ans4(matmult_1_ans4));
  assign controlled_buffer_16_out = rom_1_data[21] ? bus_terminal_1_ram_system : 16'bz;  // Controlled_Buffer controlled_buffer_16
  bus_terminal bus_terminal_1 (
    .OE(rom_1_data[26]), .B1(rom_1_data[25]), .B2(rom_1_data[24]), .Data_in(controlled_buffer_1_out),
    .RAM_Inst(bus_terminal_1_ram_inst), .RAM_System(bus_terminal_1_ram_system), .RAM_A(bus_terminal_1_ram_a),
    .RAM_B(bus_terminal_1_ram_b));
  assign controlled_buffer_17_out = rom_1_data[22] ? bus_terminal_1_ram_a : 16'bz;  // Controlled_Buffer controlled_buffer_17
  assign controlled_buffer_18_out = rom_1_data[23] ? bus_terminal_1_ram_b : 16'bz;  // Controlled_Buffer controlled_buffer_18
  RAM #(.addrWidth(5), .dataWidth(16), .\type ("nonvolatile")) ram_2 (
    .addr(counter_3_q), .we(rom_1_data[62]), .oe(rom_1_data[63]), .clk(clock_1_out),
    .din(controlled_buffer_17_out), .dout(ram_2_dout));
  // Probe on ram_1_dout
  Register #(.width(16)) matmult_output (
    .D(matmult_1_ans1), .en(rom_1_data[2]), .clk(clock_1_out), .Q(matmult_output_q));  // open: clr
  RAM #(.addrWidth(5), .dataWidth(16)) ram_3 (
    .addr(counter_2_q), .we(rom_1_data[56]), .oe(rom_1_data[57]), .clk(clock_1_out),
    .din(controlled_buffer_16_out), .dout(ram_3_dout));
  Register #(.width(16)) register_13 (
    .D(matmult_1_ans2), .en(rom_1_data[2]), .clk(clock_1_out), .Q(register_13_q));  // open: clr
  assign controlled_buffer_1_out = rom_1_data[7] ? matmult_output_q : 16'bz;  // Controlled_Buffer controlled_buffer_19
  // Probe on ram_2_dout
  Register #(.width(16)) register_14 (
    .D(matmult_1_ans3), .en(rom_1_data[2]), .clk(clock_1_out), .Q(register_14_q));  // open: clr
  assign controlled_buffer_1_out = rom_1_data[6] ? register_13_q : 16'bz;  // Controlled_Buffer controlled_buffer_20
  assign controlled_buffer_1_out = rom_1_data[5] ? register_14_q : 16'bz;  // Controlled_Buffer controlled_buffer_21
  // Probe on ram_3_dout
  assign controlled_buffer_7_out = rom_1_data[1] ? ram_3_dout : 16'bz;  // Controlled_Buffer controlled_buffer_22
  Register #(.width(16)) register_15 (
    .D(matmult_1_ans4), .en(rom_1_data[2]), .clk(clock_1_out), .Q(register_15_q));  // open: clr
  RAM #(.addrWidth(5), .dataWidth(16), .\type ("nonvolatile")) ram_4 (
    .addr(counter_4_q), .we(rom_1_data[60]), .oe(rom_1_data[61]), .clk(clock_1_out),
    .din(controlled_buffer_18_out), .dout(ram_4_dout));
  assign controlled_buffer_1_out = rom_1_data[4] ? register_15_q : 16'bz;  // Controlled_Buffer controlled_buffer_23
  // Probe on ram_4_dout
  ROM #(.addrWidth(9), .dataWidth(64)) rom_1 (.addr({register_1_q[4:0], ROM_Clock_Counter_q}), .data(rom_1_data));
  not not_1 (not_1_out, rom_1_data[17]);
  Counter #(.max('hf), .width(4)) ROM_Clock_Counter (
    .up(not_1_out), .count(not_1_out), .clk(clock_1_out), .Q(ROM_Clock_Counter_q));  // open: clr, load, D, carry
  // also tied to GND on the sheet: controlled_buffer_2_out_2[5]

  // Notes on the sheet:
  //   Current Opcode
  //   MAR_zero
  //   Reg 1
  //   Reg 3
  //   Reg 5
  //   Reg 7
  //   Reg 6
  //   Reg 2
  //   Reg 4
  //   Reg 8
  //   MAR_A
  //   MBR_Z
  //   MBR_A
  //   MBR_B
  //   MAR_B
  //   inst
  //   System
  //   Current opcode
  //   halt
  //   contents of rom_1 (hex, n*v repeats v):
  //   0 822000000000000 822000000000000 12000000000000 c00000000000 a0cc000000000000 a0cc000000000000
  //   c280810000000 3890000000 7*0 1000000000000 100000005240000 600000000 822000000000000 822000000000000
  //   12000000000000 80000000 0 0 3808040800 600000000 822000000000000 822000000000000 12000000000000
  //   1c00080000000 3808040800 600000000 822000000000000 822000000000000 12000000000000 1000080000000 19*0
  //   c000810040000 600000000 c000800040000 600000000 822000000000000 822000000000000 12000000000000
  //   1000080000000 100000005240000 600000000 822000000000000 822000000000000 12000000000000 c00000000000
  //   a0cc000000000000 a0cc000000000000 c280810000000 3890000000 1000000000000 4*0 40000000040000
  //   a0cc000000000000 a0cc000000000000 c280810000000 3890000000 6*0 1004000007810000 4008000606408000
  //   822000000000000 822000000000000 12000000000000 c00000000000 3890000000 4*0 c282000000000 2000004000
  //   81000000000 200600002000 822000000000000 822000000000000 12000000000000 c00000000000
  //   a0cc000000000000 a0cc000000000000 c280810000000 a0cc000000000300 a0cc000000000000 a0cc000000000300
  //   a0cc140000000000 a0cc000000000000 a0cc000000000300 a0cc014000000000 a0cc000000000300
  //   a0cc140000000000 a0cc000000000300 a0cc028000000000 a0cc000600000300 82c280000000000 822000000000000
  //   12000000000000 1000080000000 c00000000000 a0cc000000000000 a0cc000000000000 a0cc000000000000
  //   c280810000000 3890000000 0 101003005200384 300 10000300520034c 10000300520032c 10000300520031c
  //   600000000 822000000000000 822000000000000 12000000000000 3000000004 600000000 822000000000000
  //   822000000000000 12000000000000 1000080000000 0 a0cc000000000000 a0cc000000000000 0 0 0 600000000 0
  //   822000000000000 822000000000000 0 c000800040000 822000000000000 822000000000000 12000000000000
  //   80000000 4*0 c000800040000 600000000 822000000000000 822000000000000 12000000000000 1000080000000
  //   600000000 822000000000000 822000000000000 12000000000000 1000080000000 4*0 c000800040000 600000000
  //   822000000000000 820000000000000 12000000000000 1000080000000 c000800040000 600000000 822000000000000
  //   822000000000000 12000000000000 1000080000000 c00080040000 600000000 822000000000000 822000000000000
  //   12000000000000 c000800040000 600000000 822000000000000 822000000000000 12000000000000 1000080000000
  //   c000800040000 600000000 822000000000000 822000000000000 12000000000000 1000080000000 0 c000800040000
  //   0 0 c000800040000 600000000 822000000000000 820000000000000 12000000000000 1000080000000
  //   a0cc000000000000 c280810000000 3890000000 0 0 0 600000000 822000000000000 822000000000000
  //   12000000000000 c00000000000 a0cc000000000000 a0cc000000000000 c280810000000 3890000000
  //   a0cc000000000000 36*0 c000800040000 3808001000 600000000 822000000000000 822000000000000
  //   12000000000000 1000080000000 c000800040000 600000000 822000000000000 822000000000000 12000000000000
  //   1000080000000 31*0 c00000000000 a0cc000000000000 a0cc000000000000 c280810000000 3890000000 0 0 0
  //   1000000000000 100000005280000 1000000000000 100000005280000 600000000 822000000000000
  //   822000000000000 12000000000000 147*0 20000 4*0 20000 0 20000 4*0 20000
  //   ROM CONTROLLER
  //   Clock Counter
endmodule

module TwoBitAdder (
  input  A,
  input  B,
  input  carry_in,
  output sum,
  output carryout
);

  wire and_1_out, and_2_out, xor_1_out;

  xor xor_1 (xor_1_out, A, B);
  and and_1 (and_1_out, A, B);
  xor xor_2 (sum, xor_1_out, carry_in);
  and and_2 (and_2_out, xor_1_out, carry_in);
  or or_1 (carryout, and_1_out, and_2_out);

  // Notes on the sheet:
  //   intermediate sum
endmodule

module FourBitAdder (
  input  [3:0] A,
  input  Carry_in,
  input  [3:0] B,
  output [3:0] sumout,
  output carry_out
);

  wire twobitadder_1_carryout, twobitadder_2_carryout, twobitadder_4_carryout;

  // Probe on A
  // Probe on B
  TwoBitAdder twobitadder_1 (
    .A(A[0]), .B(B[0]), .carry_in(Carry_in), .sum(sumout[0]), .carryout(twobitadder_1_carryout));
  TwoBitAdder twobitadder_2 (
    .A(A[1]), .B(B[1]), .carry_in(twobitadder_1_carryout), .sum(sumout[1]), .carryout(twobitadder_2_carryout));
  TwoBitAdder twobitadder_3 (
    .A(A[3]), .B(B[3]), .carry_in(twobitadder_4_carryout), .sum(sumout[3]), .carryout(carry_out));
  // Probe on sumout
  TwoBitAdder twobitadder_4 (
    .A(A[2]), .B(B[2]), .carry_in(twobitadder_2_carryout), .sum(sumout[2]), .carryout(twobitadder_4_carryout));
endmodule

module EightBitAdder (
  input  [7:0] A,
  input  Carry_in,
  input  [7:0] B,
  output [7:0] sum,
  output carryout
);

  wire fourbitadder_1_carry_out;

  // Probe on B
  // Probe on A
  FourBitAdder fourbitadder_1 (
    .A(A[3:0]), .Carry_in(Carry_in), .B(B[3:0]), .sumout(sum[3:0]), .carry_out(fourbitadder_1_carry_out));
  FourBitAdder fourbitadder_2 (
    .A(A[7:4]), .Carry_in(fourbitadder_1_carry_out), .B(B[7:4]), .sumout(sum[7:4]), .carry_out(carryout));
  // Probe on sum
  LED led_1 ();  // open: in
endmodule

module SixteenBitAdder (
  input  [15:0] A,
  input  Carry_in,
  input  [15:0] B,
  output [15:0] sum,
  output carry_out
);

  wire eightbitadder_1_carryout;

  // Probe on B
  // Probe on A
  EightBitAdder eightbitadder_1 (
    .A(A[7:0]), .Carry_in(Carry_in), .B(B[7:0]), .sum(sum[7:0]), .carryout(eightbitadder_1_carryout));
  EightBitAdder eightbitadder_2 (
    .A(A[15:8]), .Carry_in(eightbitadder_1_carryout), .B(B[15:8]), .sum(sum[15:8]), .carryout(carry_out));
  // Probe on sum
  LED led_1 ();  // open: in
endmodule

module FourBitMultiplier (
  input  [3:0] B,
  input  [3:0] A,
  output [7:0] Product
);

  wire [2:0] and_15_out;
  wire [3:0] and_4_out, and_8_out, and_12_out, fourbitadder_1_sumout, fourbitadder_3_carry_out;

  // Probe on A
  and and_1 (and_4_out[3], A[3], B[3]);
  and and_2 (and_4_out[2], A[3], B[2]);
  and and_3 (and_4_out[1], A[3], B[1]);
  and and_4 (and_4_out[0], A[3], B[0]);
  and and_5 (and_8_out[3], A[2], B[3]);
  and and_6 (and_8_out[2], A[2], B[2]);
  and and_7 (and_8_out[1], A[2], B[1]);
  and and_8 (and_8_out[0], A[2], B[0]);
  and and_9 (and_12_out[3], A[1], B[3]);
  // Probe on Product
  // Probe on B
  and and_10 (and_12_out[1], A[1], B[1]);
  and and_11 (and_12_out[2], A[1], B[2]);
  and and_12 (and_12_out[0], A[1], B[0]);
  FourBitAdder fourbitadder_1 (
    .A(fourbitadder_3_carry_out), .Carry_in(1'b0), .B(and_8_out),
    .sumout({fourbitadder_1_sumout[2:0], Product[2]}), .carry_out(fourbitadder_1_sumout[3]));
  FourBitAdder fourbitadder_2 (
    .A(fourbitadder_1_sumout), .Carry_in(1'b0), .B(and_4_out), .sumout(Product[6:3]), .carry_out(Product[7]));
  and and_13 (and_15_out[2], A[0], B[3]);
  FourBitAdder fourbitadder_3 (
    .A({1'b0, and_15_out}), .Carry_in(1'b0), .B(and_12_out),
    .sumout({fourbitadder_3_carry_out[2:0], Product[1]}), .carry_out(fourbitadder_3_carry_out[3]));
  and and_14 (and_15_out[1], A[0], B[2]);
  and and_15 (and_15_out[0], A[0], B[1]);
  and and_16 (Product[0], A[0], B[0]);
endmodule

module Mult_8 (
  input  [7:0] A,
  input  [7:0] B,
  output [15:0] product,
  output Carry_out
);

  wire [15:0] fourbitmultiplier_1_product, sixteenbitadder_1_sum, sixteenbitadder_2_sum, undriven,
       undriven_2, undriven_3;

  // Probe on A
  // Probe on B
  // Probe on B[3:0]
  // Probe on A[3:0]
  FourBitMultiplier fourbitmultiplier_1 (.B(A[3:0]), .A(B[3:0]), .Product(fourbitmultiplier_1_product[7:0]));
  FourBitMultiplier fourbitmultiplier_2 (.B(A[3:0]), .A(B[7:4]), .Product(undriven[11:4]));
  FourBitMultiplier fourbitmultiplier_3 (.B(A[7:4]), .A(B[3:0]), .Product(undriven_2[11:4]));
  FourBitMultiplier fourbitmultiplier_4 (.B(A[7:4]), .A(B[7:4]), .Product(undriven_3[15:8]));
  // Probe on fourbitmultiplier_1_product[7:0]
  // Probe on undriven[11:4]
  // Probe on undriven_2[11:4]
  // Probe on undriven_3[15:8]
  SixteenBitAdder sixteenbitadder_1 (
    .A(fourbitmultiplier_1_product), .B(undriven), .sum(sixteenbitadder_1_sum));  // open: Carry_in, carry_out
  SixteenBitAdder sixteenbitadder_2 (
    .A(undriven_2), .B(undriven_3), .sum(sixteenbitadder_2_sum));  // open: Carry_in, carry_out
  // Probe on sixteenbitadder_1_sum
  // Probe on sixteenbitadder_2_sum
  // Probe on product
  SixteenBitAdder sixteenbitadder_3 (
    .A(sixteenbitadder_1_sum), .B(sixteenbitadder_2_sum), .sum(product), .carry_out(Carry_out));  // open: Carry_in
endmodule

module InstructionSplitter (
  input  [15:0] Instruction,
  input  Write_Enable,
  input  clock,
  output [4:0] Add_B,
  output [4:0] Add_A,
  output [4:0] Opcode,
  output flag
);

  Register #(.width(16)) register_1 (
    .D(Instruction), .en(Write_Enable), .clk(clock), .Q({flag, Opcode, Add_A, Add_B}));  // open: clr
endmodule

module TwoBitComparator (
  input  [1:0] A,
  input  [1:0] B,
  output A_equals_B,
  output A_gt_B,
  output B_gt_A
);

  wire and_1_out, and_2_out, and_3_out, and_4_out, and_5_out, and_6_out, nor_1_out, not_1_out, not_2_out,
       not_3_out, not_4_out;

  not not_1 (not_1_out, B[1]);
  not not_2 (not_2_out, A[1]);
  not not_3 (not_3_out, B[0]);
  not not_4 (not_4_out, A[0]);
  and and_1 (and_1_out, not_1_out, A[1]);
  and and_2 (and_2_out, B[1], not_2_out);
  and and_3 (and_3_out, not_3_out, A[0]);
  and and_4 (and_4_out, B[0], not_4_out);
  nor nor_1 (nor_1_out, and_1_out, and_2_out);
  and and_5 (and_5_out, nor_1_out, and_3_out);
  and and_6 (and_6_out, nor_1_out, and_4_out);
  or or_1 (A_gt_B, and_1_out, and_5_out);
  or or_2 (B_gt_A, and_6_out, and_2_out);
  nor nor_2 (A_equals_B, A_gt_B, B_gt_A);
endmodule

module comparator_4 (
  input  [3:0] A,
  input  [3:0] B,
  output A_equals_B,
  output A_gt_B,
  output B_gt_A
);

  wire and_1_out, and_3_out, twobitcomparator_1_a_equals_b, twobitcomparator_1_a_gt_b,
       twobitcomparator_1_b_gt_a, twobitcomparator_2_a_equals_b, twobitcomparator_2_a_gt_b,
       twobitcomparator_2_b_gt_a;

  TwoBitComparator twobitcomparator_1 (
    .A(A[1:0]), .B(B[1:0]), .A_equals_B(twobitcomparator_1_a_equals_b), .A_gt_B(twobitcomparator_1_a_gt_b),
    .B_gt_A(twobitcomparator_1_b_gt_a));
  TwoBitComparator twobitcomparator_2 (
    .A(A[3:2]), .B(B[3:2]), .A_equals_B(twobitcomparator_2_a_equals_b), .A_gt_B(twobitcomparator_2_a_gt_b),
    .B_gt_A(twobitcomparator_2_b_gt_a));
  and and_1 (and_1_out, twobitcomparator_1_b_gt_a, twobitcomparator_2_a_equals_b);
  and and_2 (A_equals_B, twobitcomparator_1_a_equals_b, twobitcomparator_2_a_equals_b);
  and and_3 (and_3_out, twobitcomparator_2_a_equals_b, twobitcomparator_1_a_gt_b);
  or or_1 (B_gt_A, and_1_out, twobitcomparator_2_b_gt_a);
  or or_2 (A_gt_B, twobitcomparator_2_a_gt_b, and_3_out);
endmodule

module comparator_8 (
  input  [7:0] A,
  input  [7:0] B,
  output A_equals_B,
  output A_gt_B,
  output B_gt_A
);

  wire and_1_out, and_3_out, comparator_4_1_a_equals_b, comparator_4_1_a_gt_b, comparator_4_1_b_gt_a,
       comparator_4_2_a_equals_b, comparator_4_2_a_gt_b, comparator_4_2_b_gt_a;

  comparator_4 comparator_4_1 (
    .A(A[3:0]), .B(B[3:0]), .A_equals_B(comparator_4_1_a_equals_b), .A_gt_B(comparator_4_1_a_gt_b),
    .B_gt_A(comparator_4_1_b_gt_a));
  comparator_4 comparator_4_2 (
    .A(A[7:4]), .B(B[7:4]), .A_equals_B(comparator_4_2_a_equals_b), .A_gt_B(comparator_4_2_a_gt_b),
    .B_gt_A(comparator_4_2_b_gt_a));
  and and_1 (and_1_out, comparator_4_1_b_gt_a, comparator_4_2_a_equals_b);
  and and_2 (A_equals_B, comparator_4_1_a_equals_b, comparator_4_2_a_equals_b);
  and and_3 (and_3_out, comparator_4_2_a_equals_b, comparator_4_1_a_gt_b);
  or or_1 (B_gt_A, and_1_out, comparator_4_2_b_gt_a);
  or or_2 (A_gt_B, comparator_4_2_a_gt_b, and_3_out);
endmodule

module comparator_16 (
  input  [15:0] A,
  input  [15:0] B,
  output [15:0] out_3
);

  wire and_1_out, and_3_out, comparator_8_1_a_equals_b, comparator_8_1_a_gt_b, comparator_8_1_b_gt_a,
       comparator_8_2_a_equals_b, comparator_8_2_a_gt_b, comparator_8_2_b_gt_a;

  comparator_8 comparator_8_1 (
    .A(A[7:0]), .B(B[7:0]), .A_equals_B(comparator_8_1_a_equals_b), .A_gt_B(comparator_8_1_a_gt_b),
    .B_gt_A(comparator_8_1_b_gt_a));
  comparator_8 comparator_8_2 (
    .A(A[15:8]), .B(B[15:8]), .A_equals_B(comparator_8_2_a_equals_b), .A_gt_B(comparator_8_2_a_gt_b),
    .B_gt_A(comparator_8_2_b_gt_a));
  and and_1 (and_1_out, comparator_8_1_b_gt_a, comparator_8_2_a_equals_b);
  and and_2 (out_3[1], comparator_8_1_a_equals_b, comparator_8_2_a_equals_b);
  and and_3 (and_3_out, comparator_8_2_a_equals_b, comparator_8_1_a_gt_b);
  or or_1 (out_3[0], and_1_out, comparator_8_2_b_gt_a);
  or or_2 (out_3[2], comparator_8_2_a_gt_b, and_3_out);
  // Probe on {{13{1'b0}}, out_3[2:0]}

  assign out_3[15:3] = {13{1'b0}};

  // Notes on the sheet:
  //   A=B
  //   B>A
  //   A>B
  //   Key:-
  //   A > B : 4
  //   A = B : 2
  //   A < B : 1
endmodule

module ALU (
  input  [15:0] A,
  input  [4:0] opcode,
  input  [15:0] B,
  output [15:0] out_4,
  output overflow,
  output overflow_sub
);

  wire [7:0] bitselector_1_out, bitselector_2_out;
  wire [15:0] and_1_out, comparator_16_1_out_3, mult_8_1_product, not_1_out, sixteenbitadder_1_sum,
       sub_16_1_sum, undriven, xor_1_out;

  BitSelector #(.group(8), .width(16)) bitselector_1 (.in(A), .out(bitselector_1_out), .sel(1'b0));
  BitSelector #(.group(8), .width(16)) bitselector_2 (.in(B), .out(bitselector_2_out), .sel(1'b0));
  assign and_1_out = A & B;  // AND_Gate and_1, 16 bits wide
  assign not_1_out = ~A;  // NOT_Gate not_1, 16 bits wide
  Mult_8 mult_8_1 (.A(bitselector_1_out), .B(bitselector_2_out), .product(mult_8_1_product));  // open: Carry_out
  comparator_16 comparator_16_1 (.A(A), .B(B), .out_3(comparator_16_1_out_3));
  SixteenBitAdder sixteenbitadder_1 (.A(A), .Carry_in(1'b0), .B(B), .sum(sixteenbitadder_1_sum), .carry_out(overflow));
  sub_16 sub_16_1 (.A(A), .B(B), .sum(sub_16_1_sum), .carry_out(overflow_sub));
  assign xor_1_out = A ^ B;  // XOR_Gate xor_1, 16 bits wide
  mux_32 mux_32_1 (
    .in_1(opcode), .Addition(sixteenbitadder_1_sum), .Multiplication(mult_8_1_product),
    .Subtraction(sub_16_1_sum), .Logical_AND(and_1_out), .Logical_NOT(not_1_out), .D16(undriven),
    .Comparison(comparator_16_1_out_3), .Logical_XOR(xor_1_out), .out_34(out_4));  // open: Reserved, D2, D3, D4, D5, D8, D9, D11, D13, D15, D17, D19, D20, D21, D22, D24, D25, D26, D27, D28, D29, D30, D31, D32
  // Probe on out_4
endmodule

module decoder_5x32 (
  input  [4:0] Flag_opcode
);

  wire and_1_out, and_2_out, and_3_out, and_4_out, and_5_out, and_6_out, and_7_out, and_8_out, and_9_out,
       and_10_out, and_11_out, and_12_out, and_13_out, and_14_out, and_15_out, and_16_out, and_17_out,
       and_18_out, and_19_out, and_20_out, and_21_out, and_22_out, and_23_out, and_24_out, and_25_out,
       and_26_out, and_27_out, and_28_out, and_29_out, and_30_out, and_31_out, and_32_out, not_1_out,
       not_2_out, not_3_out, not_4_out, not_5_out;

  not not_1 (not_1_out, Flag_opcode[4]);
  not not_2 (not_2_out, Flag_opcode[3]);
  not not_3 (not_3_out, Flag_opcode[2]);
  not not_4 (not_4_out, Flag_opcode[1]);
  not not_5 (not_5_out, Flag_opcode[0]);
  and and_1 (and_1_out, not_1_out, not_2_out, not_3_out, not_4_out, Flag_opcode[0]);
  and and_2 (and_2_out, not_1_out, not_2_out, not_3_out, Flag_opcode[1], not_5_out);
  and and_3 (and_3_out, not_1_out, not_2_out, not_3_out, Flag_opcode[1], Flag_opcode[0]);
  and and_4 (and_4_out, not_1_out, not_2_out, Flag_opcode[2], not_4_out, not_5_out);
  and and_5 (and_5_out, not_1_out, not_2_out, Flag_opcode[2], not_4_out, Flag_opcode[0]);
  and and_6 (and_6_out, not_1_out, not_2_out, Flag_opcode[2], Flag_opcode[1], not_5_out);
  and and_7 (and_7_out, not_1_out, not_2_out, Flag_opcode[2], Flag_opcode[1], Flag_opcode[0]);
  and and_8 (and_8_out, not_1_out, Flag_opcode[3], not_3_out, not_4_out, not_5_out);
  and and_9 (and_9_out, not_1_out, Flag_opcode[3], not_3_out, not_4_out, Flag_opcode[0]);
  and and_10 (and_10_out, not_1_out, Flag_opcode[3], not_3_out, Flag_opcode[1], not_5_out);
  and and_11 (and_11_out, not_1_out, Flag_opcode[3], not_3_out, Flag_opcode[1], Flag_opcode[0]);
  and and_12 (and_12_out, not_1_out, Flag_opcode[3], Flag_opcode[2], not_4_out, not_5_out);
  and and_13 (and_13_out, not_1_out, Flag_opcode[3], Flag_opcode[2], not_4_out, Flag_opcode[0]);
  and and_14 (and_14_out, not_1_out, Flag_opcode[3], Flag_opcode[2], Flag_opcode[1], not_5_out);
  and and_15 (and_15_out, not_1_out, Flag_opcode[3], Flag_opcode[2], Flag_opcode[1], Flag_opcode[0]);
  and and_16 (and_16_out, not_1_out, not_2_out, not_3_out, not_4_out, not_5_out);
  and and_17 (and_17_out, Flag_opcode[4], not_2_out, not_3_out, not_4_out, Flag_opcode[0]);
  and and_18 (and_18_out, Flag_opcode[4], not_2_out, not_3_out, Flag_opcode[1], not_5_out);
  and and_19 (and_19_out, Flag_opcode[4], not_2_out, not_3_out, Flag_opcode[1], Flag_opcode[0]);
  and and_20 (and_20_out, Flag_opcode[4], not_2_out, Flag_opcode[2], not_3_out, not_5_out);
  and and_21 (and_21_out, Flag_opcode[4], not_2_out, Flag_opcode[2], not_4_out, Flag_opcode[0]);
  and and_22 (and_22_out, Flag_opcode[4], not_2_out, Flag_opcode[2], Flag_opcode[1], not_5_out);
  and and_23 (and_23_out, Flag_opcode[4], not_2_out, Flag_opcode[2], Flag_opcode[1], Flag_opcode[0]);
  and and_24 (and_24_out, Flag_opcode[4], Flag_opcode[4], not_3_out, not_4_out, not_5_out);
  and and_25 (and_25_out, Flag_opcode[4], Flag_opcode[4], not_3_out, not_4_out, Flag_opcode[0]);
  and and_26 (and_26_out, Flag_opcode[4], Flag_opcode[4], not_3_out, Flag_opcode[1], not_5_out);
  and and_27 (and_27_out, Flag_opcode[4], Flag_opcode[4], not_3_out, Flag_opcode[1], Flag_opcode[0]);
  and and_28 (and_28_out, Flag_opcode[4], Flag_opcode[4], Flag_opcode[2], not_4_out, not_5_out);
  and and_29 (and_29_out, Flag_opcode[4], Flag_opcode[4], Flag_opcode[2], not_4_out, Flag_opcode[0]);
  and and_30 (and_30_out, Flag_opcode[4], Flag_opcode[4], Flag_opcode[2], Flag_opcode[1], not_5_out);
  and and_31 (and_31_out, Flag_opcode[4], Flag_opcode[4], Flag_opcode[2], Flag_opcode[1], Flag_opcode[0]);
  and and_32 (and_32_out, Flag_opcode[4], not_2_out, not_3_out, not_4_out, not_5_out);

  // Notes on the sheet:
  //   F
  //   S3
  //   S2
  //   S1
  //   S0
  //   F'
  //   S3'
  //   S2'
  //   S1'
  //   S0'
  //   0001
  //   0010
  //   0011
  //   0100
  //   0101
  //   0110
  //   0111
  //   1000
  //   1001
  //   1010
  //   1011
  //   1100
  //   1101
  //   1110
  //   1111
  //   0001
  //   0010
  //   0011
  //   0100
  //   0101
  //   0110
  //   0111
  //   1000
  //   1001
  //   1010
  //   1011
  //   1100
  //   1101
  //   1110
  //   1111
  //   0000
  //   0000
endmodule

module mux_32 (
  input  [4:0] in_1,
  input  [15:0] Reserved,
  input  [15:0] D2,
  input  [15:0] D3,
  input  [15:0] D4,
  input  [15:0] D5,
  input  [15:0] Addition,
  input  [15:0] Multiplication,
  input  [15:0] D8,
  input  [15:0] D9,
  input  [15:0] Subtraction,
  input  [15:0] D11,
  input  [15:0] Logical_AND,
  input  [15:0] D13,
  input  [15:0] Logical_NOT,
  input  [15:0] D15,
  input  [15:0] D16,
  input  [15:0] D17,
  input  [15:0] Comparison,
  input  [15:0] D19,
  input  [15:0] D20,
  input  [15:0] D21,
  input  [15:0] D22,
  input  [15:0] Logical_XOR,
  input  [15:0] D24,
  input  [15:0] D25,
  input  [15:0] D26,
  input  [15:0] D27,
  input  [15:0] D28,
  input  [15:0] D29,
  input  [15:0] D30,
  input  [15:0] D31,
  input  [15:0] D32,
  output [15:0] out_34
);

  wire [15:0] and_1_out, and_2_out, and_3_out, and_4_out, and_5_out, and_6_out, and_7_out, and_8_out,
       and_9_out, and_10_out, and_11_out, and_12_out, and_13_out, and_14_out, and_15_out, and_16_out,
       and_17_out, and_18_out, and_19_out, and_20_out, and_21_out, and_22_out, and_23_out, and_24_out,
       and_25_out, and_26_out, and_27_out, and_28_out, and_29_out, and_30_out, and_31_out, and_32_out,
       bit_extender_1_out, bit_extender_2_out, bit_extender_3_out, bit_extender_4_out, bit_extender_5_out,
       not_1_out, not_2_out, not_3_out, not_4_out, not_5_out;

  assign bit_extender_1_out = {{15{in_1[3]}}, in_1[3]};  // Bit_Extender bit_extender_1
  assign bit_extender_2_out = {{15{in_1[4]}}, in_1[4]};  // Bit_Extender bit_extender_2
  assign bit_extender_3_out = {{15{in_1[1]}}, in_1[1]};  // Bit_Extender bit_extender_3
  assign bit_extender_4_out = {{15{in_1[2]}}, in_1[2]};  // Bit_Extender bit_extender_4
  assign not_1_out = ~bit_extender_2_out;  // NOT_Gate not_1, 16 bits wide
  assign bit_extender_5_out = {{15{in_1[0]}}, in_1[0]};  // Bit_Extender bit_extender_5
  assign not_2_out = ~bit_extender_1_out;  // NOT_Gate not_2, 16 bits wide
  assign not_3_out = ~bit_extender_4_out;  // NOT_Gate not_3, 16 bits wide
  assign not_4_out = ~bit_extender_3_out;  // NOT_Gate not_4, 16 bits wide
  assign not_5_out = ~bit_extender_5_out;  // NOT_Gate not_5, 16 bits wide
  assign and_1_out = not_5_out & not_4_out & not_2_out & not_1_out & Reserved;  // AND_Gate and_1, 16 bits wide
  assign and_2_out = not_5_out & not_4_out & not_2_out & bit_extender_2_out & D2;  // AND_Gate and_2, 16 bits wide
  assign and_3_out = not_5_out & not_4_out & bit_extender_1_out & not_1_out & D3;  // AND_Gate and_3, 16 bits wide
  assign and_4_out = not_5_out & not_4_out & not_2_out & not_1_out & D4;  // AND_Gate and_4, 16 bits wide
  assign and_5_out = not_5_out & bit_extender_3_out & not_2_out & not_1_out & D5;  // AND_Gate and_5, 16 bits wide
  assign and_6_out = bit_extender_5_out & not_4_out & not_2_out & not_1_out & Addition;  // AND_Gate and_6, 16 bits wide
  assign and_7_out = bit_extender_5_out & bit_extender_3_out & not_2_out & not_1_out & Multiplication;  // AND_Gate and_7, 16 bits wide
  assign and_8_out = bit_extender_5_out & not_4_out & not_2_out & not_1_out & D8;  // AND_Gate and_8, 16 bits wide
  assign and_9_out = bit_extender_5_out & not_4_out & bit_extender_1_out & not_1_out & D9;  // AND_Gate and_9, 16 bits wide
  assign and_10_out = bit_extender_5_out & not_4_out & not_2_out & bit_extender_2_out & Subtraction;  // AND_Gate and_10, 16 bits wide
  assign and_11_out = bit_extender_5_out & bit_extender_3_out & not_2_out & not_1_out & D11;  // AND_Gate and_11, 16 bits wide
  assign and_12_out = bit_extender_5_out & bit_extender_3_out & bit_extender_1_out & not_1_out & Logical_AND;  // AND_Gate and_12, 16 bits wide
  assign and_13_out = bit_extender_5_out & bit_extender_3_out & not_2_out & bit_extender_2_out & D13;  // AND_Gate and_13, 16 bits wide
  assign and_14_out = bit_extender_5_out & not_4_out & bit_extender_1_out & not_1_out & Logical_NOT;  // AND_Gate and_14, 16 bits wide
  assign and_15_out = bit_extender_5_out & not_4_out & not_2_out & bit_extender_2_out & D15;  // AND_Gate and_15, 16 bits wide
  assign and_16_out = bit_extender_5_out & not_4_out & bit_extender_1_out & bit_extender_2_out & D16;  // AND_Gate and_16, 16 bits wide
  assign and_17_out = not_5_out & bit_extender_3_out & not_2_out & not_1_out & D17;  // AND_Gate and_17, 16 bits wide
  assign and_18_out = not_5_out & bit_extender_3_out & bit_extender_1_out & not_1_out & Comparison;  // AND_Gate and_18, 16 bits wide
  assign and_19_out = not_5_out & bit_extender_3_out & not_2_out & bit_extender_2_out & D19;  // AND_Gate and_19, 16 bits wide
  assign and_20_out = not_5_out & bit_extender_3_out & bit_extender_1_out & not_1_out & D20;  // AND_Gate and_20, 16 bits wide
  assign and_21_out = not_5_out & bit_extender_3_out & not_2_out & bit_extender_2_out & D21;  // AND_Gate and_21, 16 bits wide
  assign and_22_out = not_5_out & bit_extender_3_out & bit_extender_1_out & bit_extender_2_out & D22;  // AND_Gate and_22, 16 bits wide
  assign and_23_out = not_5_out & not_4_out & bit_extender_1_out & not_1_out & Logical_XOR;  // AND_Gate and_23, 16 bits wide
  assign and_24_out = not_5_out & not_4_out & not_2_out & bit_extender_2_out & D24;  // AND_Gate and_24, 16 bits wide
  assign and_25_out = not_5_out & not_4_out & bit_extender_1_out & bit_extender_2_out & D25;  // AND_Gate and_25, 16 bits wide
  assign and_26_out = not_5_out & not_4_out & bit_extender_1_out & bit_extender_2_out & D26;  // AND_Gate and_26, 16 bits wide
  assign and_27_out = bit_extender_5_out & bit_extender_3_out & bit_extender_1_out & not_1_out & D27;  // AND_Gate and_27, 16 bits wide
  assign and_28_out = bit_extender_5_out & bit_extender_3_out & not_2_out & bit_extender_2_out & D28;  // AND_Gate and_28, 16 bits wide
  assign and_29_out = bit_extender_5_out & bit_extender_3_out & bit_extender_1_out & bit_extender_2_out & D29;  // AND_Gate and_29, 16 bits wide
  assign and_30_out = bit_extender_5_out & not_4_out & bit_extender_1_out & bit_extender_2_out & D30;  // AND_Gate and_30, 16 bits wide
  assign and_31_out = not_5_out & bit_extender_3_out & bit_extender_1_out & bit_extender_2_out & D31;  // AND_Gate and_31, 16 bits wide
  assign and_32_out = bit_extender_5_out & bit_extender_3_out & bit_extender_1_out & bit_extender_2_out & D32;  // AND_Gate and_32, 16 bits wide
  assign out_34 = and_1_out | and_2_out | and_3_out | and_4_out | and_5_out | and_6_out | and_7_out | and_8_out | and_9_out | and_10_out | and_11_out | and_12_out | and_13_out | and_14_out | and_15_out | and_16_out | and_17_out | and_18_out | and_19_out | and_20_out | and_21_out | and_22_out | and_23_out | and_24_out | and_25_out | and_26_out | and_27_out | and_28_out | and_29_out | and_30_out | and_31_out | and_32_out;  // OR_Gate or_1, 16 bits wide

  // Notes on the sheet:
  //   E
  //   D
  //   C
  //   E'
  //   B
  //   D'
  //   A
  //   C'
  //   B'
  //   A'
  //   A'B'C'D'E'
  //   A'B'C'D'E
  //   A'B'C'DE'
  //   A'B'CD'E'
  //   A'BC'D'E'
  //   AB'C'D'E'
  //   ABC'D'E'
  //   AB'CD'E'
  //   AB'C'DE'
  //   AB'C'D'E
  //   ABCD'E'
  //   ABC'DE'
  //   ABC'D'E
  //   AB'CDE'
  //   AB'CD'E
  //   AB'C'DE
  //   A'BCD'E'
  //   A'BC'DE'
  //   A'BC'D'E
  //   A'BCDE'
  //   A'BCD'E
  //   A'BC'DE
  //   A'B'C'D'E'
  //   A'B'C'D'E'
  //   A'B'CDE
  //   A'B'C'DE
  //   ABCDE'
  //   ABCD'E
  //   ABC'DE
  //   AB'CDE
  //   A'BCDE
  //   ABCDE
endmodule

module bus_terminal (
  input  OE,
  input  B1,
  input  B2,
  input  [15:0] Data_in,
  output [15:0] RAM_Inst,
  output [15:0] RAM_System,
  output [15:0] RAM_A,
  output [15:0] RAM_B
);

  wire [15:0] and_1_out, and_2_out, and_3_out, and_4_out, bit_extender_1_out, bit_extender_2_out,
       bit_extender_3_out, not_1_out, not_2_out;

  assign bit_extender_1_out = {{15{OE}}, OE};  // Bit_Extender bit_extender_1
  assign bit_extender_2_out = {{15{B1}}, B1};  // Bit_Extender bit_extender_2
  assign bit_extender_3_out = {{15{B2}}, B2};  // Bit_Extender bit_extender_3
  assign not_1_out = ~bit_extender_2_out;  // NOT_Gate not_1, 16 bits wide
  assign not_2_out = ~bit_extender_3_out;  // NOT_Gate not_2, 16 bits wide
  assign and_1_out = not_1_out & Data_in & not_2_out;  // AND_Gate and_1, 16 bits wide
  assign and_2_out = not_1_out & Data_in & bit_extender_3_out;  // AND_Gate and_2, 16 bits wide
  assign and_3_out = bit_extender_2_out & Data_in & not_2_out;  // AND_Gate and_3, 16 bits wide
  assign and_4_out = bit_extender_2_out & Data_in & bit_extender_3_out;  // AND_Gate and_4, 16 bits wide
  assign RAM_Inst = and_1_out & bit_extender_1_out;  // AND_Gate and_5, 16 bits wide
  assign RAM_System = and_2_out & bit_extender_1_out;  // AND_Gate and_6, 16 bits wide
  assign RAM_A = and_3_out & bit_extender_1_out;  // AND_Gate and_7, 16 bits wide
  assign RAM_B = bit_extender_1_out & and_4_out;  // AND_Gate and_8, 16 bits wide
endmodule

module sub_16 (
  input  [15:0] A,
  input  [15:0] B,
  output [15:0] sum,
  output carry_out
);

  wire sixteenbitadder_2_p4;
  wire [15:0] not_1_out, sixteenbitadder_2_p6;

  // Probe on B
  // Probe on A
  assign not_1_out = ~B;  // NOT_Gate not_1, 16 bits wide
  SixteenBitAdder sixteenbitadder_1 (
    .A(A), .Carry_in(1'b0), .B(sixteenbitadder_2_p6), .sum(sum), .carry_out(carry_out));
  // SixteenBitAdder sixteenbitadder_2: pin names not known; wires that end beside it: not_1_out, 1'b0, 16'h1, sixteenbitadder_2_p4, sixteenbitadder_2_p4, sixteenbitadder_2_p6
  // Probe on sum
endmodule

module mux_2to1 (
  input  sign,
  input  [4:0] Address,
  input  [4:0] counter,
  output [4:0] out_4
);

  wire [4:0] and_1_out, and_2_out, bit_extender_1_out, not_1_out;

  assign bit_extender_1_out = {{4{sign}}, sign};  // Bit_Extender bit_extender_1
  assign not_1_out = ~bit_extender_1_out;  // NOT_Gate not_1, 5 bits wide
  assign and_1_out = not_1_out & Address;  // AND_Gate and_1, 5 bits wide
  assign and_2_out = bit_extender_1_out & counter;  // AND_Gate and_2, 5 bits wide
  assign out_4 = and_1_out | and_2_out;  // OR_Gate or_1, 5 bits wide

  // Notes on the sheet:
  //   signal 0 primary
  //   signal 1 counter
endmodule

module matmult (
  input  [15:0] reg1,
  input  [15:0] reg2,
  input  [15:0] reg3,
  input  [15:0] reg4,
  input  [15:0] reg5,
  input  [15:0] reg6,
  input  [15:0] reg7,
  input  [15:0] reg8,
  output [15:0] ans1,
  output [15:0] ans2,
  output [15:0] ans3,
  output [15:0] ans4
);

  wire [15:0] mult_8_1_product, mult_8_2_product, mult_8_3_product, mult_8_4_product, mult_8_5_product,
       mult_8_6_product, mult_8_7_product, mult_8_8_product;

  Mult_8 mult_8_1 (.A(reg1[7:0]), .B(reg5[7:0]), .product(mult_8_1_product));  // open: Carry_out
  Mult_8 mult_8_2 (.A(reg2[7:0]), .B(reg7[7:0]), .product(mult_8_2_product));  // open: Carry_out
  Mult_8 mult_8_3 (.A(reg1[7:0]), .B(reg6[7:0]), .product(mult_8_3_product));  // open: Carry_out
  Mult_8 mult_8_4 (.A(reg2[7:0]), .B(reg8[7:0]), .product(mult_8_4_product));  // open: Carry_out
  Mult_8 mult_8_5 (.A(reg3[7:0]), .B(reg5[7:0]), .product(mult_8_5_product));  // open: Carry_out
  Mult_8 mult_8_6 (.A(reg4[7:0]), .B(reg7[7:0]), .product(mult_8_6_product));  // open: Carry_out
  Mult_8 mult_8_7 (.A(reg3[7:0]), .B(reg6[7:0]), .product(mult_8_7_product));  // open: Carry_out
  Mult_8 mult_8_8 (.A(reg4[7:0]), .B(reg8[7:0]), .product(mult_8_8_product));  // open: Carry_out
  SixteenBitAdder sixteenbitadder_1 (
    .A(mult_8_1_product), .B(mult_8_2_product), .sum(ans1));  // open: Carry_in, carry_out
  SixteenBitAdder sixteenbitadder_2 (
    .A(mult_8_3_product), .B(mult_8_4_product), .sum(ans2));  // open: Carry_in, carry_out
  SixteenBitAdder sixteenbitadder_3 (
    .A(mult_8_5_product), .B(mult_8_6_product), .sum(ans3));  // open: Carry_in, carry_out
  SixteenBitAdder sixteenbitadder_4 (
    .A(mult_8_7_product), .B(mult_8_8_product), .sum(ans4));  // open: Carry_in, carry_out
endmodule
